# Fritzing sketch arm_cannon (saved by Fritzing 0.9.9b)
breadboards: 1

parts:
  Part1 = Adafruit Metro with Headers [part_number="Adafruit #2488"]
  S1 = Pushbutton [package="[THT]"]  # not connected
  LED1 = smd LED [color="Green (555nm)" package="0805 [SMD]"]
  LED2 = smd LED [color="Red (633nm)" package="0805 [SMD]"]
  LED3 = smd LED [color="Red (633nm)" package="0805 [SMD]"]
  J1 = Basic Force Sensing Resistor (FSR) [package=THT]
  R1 = Resistor [tolerance=±5% resistance=220 package="1206 [SMD]"]
  R2 = Resistor [tolerance=±5% resistance=220 package="1206 [SMD]"]
  R3 = Resistor [tolerance=±5% resistance=220 package="1206 [SMD]"]
  MOTOR1 = Vibration Motor

nets:
  N1: Part1.AD0, J1.pin_0
  N2: Part1.GND, MOTOR1.NEG
  N3: Part1.IO5, MOTOR1.POS
  N4: Part1.IO4, LED1.anode
  N5: Part1.IO3, LED2.anode
  N6: Part1.IO2, LED3.anode
  N7: Part1.+5V, J1.pin_1, R1.Pin_0, R2.Pin_0
  N8: LED1.cathode, R1.Pin_1
  N9: LED2.cathode, R2.Pin_1
  N10: LED3.cathode, R3.Pin_1

custom parts:
  Adafruit Metro with Headers: We sure love the ATmega328 here at Adafruit, and we use them a lot for our own projects. The processor has plenty of GPIO, Analog inputs, hardware UART SPI and I2C, timers and PWM galore - just enough for most simple projects. When we need to go small, we use a Pro Trinket 3V or 5V, but when size isn't as much of a concern, and an USB-serial converter is required, we reach for an Adafruit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
  Vibration Motor: An eccentric vibration motor!
